# Fritzing sketch Greenhouse System (saved by Fritzing 1.0.5)
breadboards: 1

parts:
  IR1 = vs1838b [package=THT]
  Part1 = Arduino Uno (Rev3) - ICSP
  DHT1 = DHT11 Humitidy and Temperature Sensor (3 pins)
  Part2 = FC-28 Soil Hygrometer Module
  Part3 = FC-28 Soil Hygrometer Module - Probe
  LCM1602_IIC1 = LCM1602 IIC [part_number="LCM1602 IIC" chip_label="LCM1602 IIC" package="DIP (Dual Inline) [THT]"]
  U1 = LCD-16X2 [package=lcd-16x2]

nets:
  GND: IR1.GND, Part1.GND, DHT1.Gnd, Part2.GND
  N1: IR1.Vs, Part1.D4
  5V: IR1.Data, Part1.5V, DHT1.Signal, Part2.VCC
  N2: Part1.A0, Part2.DO
  N3: Part1.A4/SDA, LCM1602_IIC1.SDA
  N4: Part1.A5/SCL, LCM1602_IIC1.SCL
  N5: Part1.D2, DHT1.Plus
  N6: Part2.POS, Part3.POS
  N7: Part2.NEG, Part3.NEG
  VSS: LCM1602_IIC1.VSS, U1.VSS
  VDD: LCM1602_IIC1.VDD, U1.VDD
  N8: LCM1602_IIC1.V0, U1.VO
  N9: LCM1602_IIC1.RS, U1.RS
  N10: LCM1602_IIC1.RW, U1.R_W
  N11: LCM1602_IIC1.E, U1.E
  N12: LCM1602_IIC1.D0, U1.DB0
  N13: LCM1602_IIC1.D1, U1.DB1
  N14: LCM1602_IIC1.D2, U1.DB2
  N15: LCM1602_IIC1.D3, U1.DB3
  N16: LCM1602_IIC1.D4, U1.DB4
  N17: LCM1602_IIC1.D5, U1.DB5
  N18: LCM1602_IIC1.D6, U1.DB6
  N19: LCM1602_IIC1.D7, U1.DB7
  N20: LCM1602_IIC1.A, U1.A
  N21: LCM1602_IIC1.K, U1.K
  N22: LCM1602_IIC1.LED_A, LCM1602_IIC1.LED_B

custom parts:
  DHT11 Humitidy and Temperature Sensor (3 pins): DHT11 Humidity and Temperature Sensor (3 pins).
  FC-28 Soil Hygrometer Module: The FC-28 is a soil hygrometer module that uses the Texas Instruments LM393 comparator chip to provide an analog measurement of soil humidity. The digital output is high when soil moisture is over a certain threshold, as determined by adjusting the potentiometer.
  FC-28 Soil Hygrometer Module - Probe: The FC-28 is a soil hygrometer module that uses the Texas Instruments LM393 comparator chip to provide an analog measurement of soil humidity.
  LCM1602 IIC: I2C-Module to use a 1602 or 2004 LCD on with the wire.h libory Serial LCD Modul

// code stored in the sketch: Main.ino
//Greenhouse Management System by Aidan Makumbe RT 

#include <IRremote.h> // Responsible for interfacing with the IR Sensor VS1838B
#include "DHT.h" //Interfacing with Temperature and Humidity Sensor DHT11
#include <LiquidCrystal_I2C.h>//For interfacing with the LCD

//Defining pins and Variables
#define DHT_TYPE DHT11
const int DHT_PIN = 2;
//const int RECV_PIN= 4;
const int moistureSensor = A0;
const float maximumMoistureLevel = 156;
float currentMoistureLevel;
float moisture;

//Configuration of Sensors and Devices
//IRrecv irrecv(RECV_PIN);
//decode_results results;
DHT dht(DHT_PIN, DHT_TYPE);
LiquidCrystal_I2C lcd(0x3F, 16, 2);


byte emptyDroplet[8] = {
  B00100,  //    ▓
  B00100,  //    ▓
  B01010,  //  ▓   ▓
  B10001,  // ▓     ▓
  B10001,  // ▓     ▓
  B10001,  // ▓     ▓
  B01110,  //   ▓▓▓   Empty 
  B00000   //
};

byte lowDroplet[8] = {
  B00100,  //    ▓
  B00100,  //    ▓
  B01010,  //   ▓ ▓
  B10001,  //  ▓   ▓
  B10001,  // ▓     ▓
  B10001,  // ▓     ▓
  B01110,  //   ▓▓▓
  B00100   //    ▓    Small low fill
};

byte mediumDroplet[8] = {
  B00100,  //   ▓
  B00100,  //   ▓
  B01010,  // ▓   ▓
  B10001,  //▓     ▓
  B10001,  //▓▓▓▓▓▓▓
  B01110,  // ▓▓▓▓▓ 
  B01110,  //   ▓     Mid fill line
  B00100
};

byte fullDroplet[8] = {
  B00100, //      ▓   
  B00100, //      ▓       
  B01110, //    ▓▓▓▓▓   
  B11111, //   ▓▓▓▓▓▓▓ 
  B11111, //  ▓▓▓▓▓▓▓▓▓
  B11111, //   ▓▓▓▓▓▓▓
  B01110, //    ▓▓▓▓▓
  B00100  //      ▓   Full Fill
};

void setup(){
  // Configuring I/O pins
  pinMode(moistureSensor, INPUT);
  //maximumMoistureLevel = analogRead(moistureSensor); //Setup 

  // Starting up Essential Services
  Serial.begin(9600);
  dht.begin(); // Starting DHT services
  //irrecv.enableIRIn(); // Enable IR Reciever

  // Initialize LCD
  lcd.init();         
  lcd.backlight();

  // Create custom characters in CGRAM (slots 0–3)
  lcd.createChar(0, emptyDroplet);
  lcd.createChar(1, lowDroplet);
  lcd.createChar(2, mediumDroplet);
  lcd.createChar(3, fullDroplet);
  
  lcd.setCursor(5, 0);
  lcd.print("Welcome");
  lcd.setCursor(7, 1);
  lcd.print("To");
  delay(2000);
  lcd.clear();

  lcd.setCursor(5, 0);
  lcd.print("Greenhouse");
  lcd.setCursor(3, 1);
  lcd.print("System");
  delay(2000);
  lcd.clear();

}

void loop(){
  int temp = dht.readTemperature();
  int hum = dht.readHumidity();

  currentMoistureLevel = analogRead(moistureSensor);
moisture = currentMoistureLevel / maximumMoistureLevel;
  

  //Print Value of Data recieved by IR sensor
  //if(irrecv.decode(&results))
 // {
    //Serial.println(results.value, HEX); // Displays recieved IR code in HEX
    //irrecv.resume();
 // }

  if( moisture <= 0.1){
    //  Execute if the Moisture is below 10%
    lcd.setCursor(11,0);
    lcd.write(byte(0)); //Special Character for moisture 
  }
  else if( moisture <= 0.3 && moisture >0.1 ){
    // Execute if the Moisture is between 10% and 30%
    lcd.setCursor(11,0);
    lcd.write(byte(1)); //Special Character for moisture 
  }
  else if(moisture <= 0.6 && moisture > 0.3){
    // Execute if the Moisture is between 30% and 60%
    lcd.setCursor(11,0);
    lcd.write(byte(2)); //Special Character for moisture 
  }
  else{
    // Otherwise the moisture level is above 60% and therefore its good enough
    lcd.setCursor(11,0);
    lcd.write(byte(3)); //Special Character for moisture 
  }

  //Refreshing the LCD input
  lcd.setCursor(0,0);
  lcd.print("Moist:");
  lcd.print(moisture*100);
  lcd.setCursor(8,1);
  lcd.print("Temp:");
  lcd.print(temp);
  lcd.print("C");
  lcd.setCursor(0,1);
  lcd.print("Hum:");
  lcd.print(hum);
  lcd.print("%");


  //Output to Serial
  Serial.print("Temp: ");
  Serial.print(temp);
  Serial.print(" ˚C | Humidity: ");
  Serial.print(hum);
  Serial.print(" % |");
  Serial.print(" Moisture: ");
  Serial.print(moisture*100);
  Serial.println("%");
  delay(2000);

}

// code stored in the sketch: Untitled2.ino
#include <IRremote.h>
